# Fritzing sketch iot_makerspace_lasercutter (saved by Fritzing 0.9.3b)
circuit board: 8.46667cm x 5.64444cm
breadboards: 1

parts:
  ADC1 = MCP3008 [package=dil16]
  ADC2 = MCP3008 [package=dil16]
  S9 = KY-026
  S8 = KY-026
  S7 = KY-026
  S6 = KY-026
  S5 = KY-026
  S4 = KY-026
  S3 = KY-026
  S10 = KY-026
  S2 = KY-026
  S11 = KY-026
  S12 = KY-026
  S1 = KY-026
  Transmitter = RF-LINK_TX [package=rf-link_tx]
  Buzzer = Piezo Speaker
  R2 = Resistor [tolerance=±5% resistance=10k package=THT]
  R3 = Resistor [tolerance=±5% resistance=10k package=THT]
  C1 = Electrolytic Capacitor [capacitance=10µF package="100 mil [THT, electrolytic]"]
  SCT013 = Microphone
  R1 = Resistor [tolerance=±5% resistance=33 package="1206 [SMD]"]
  ESP32 = ESP32 DevKit C [package="DIP (Dual Inline) [THT]"]

nets:
  N1: ADC1.CH0, S8.pin1
  N2: ADC1.CH1, S7.pin1
  N3: ADC1.CH2, S6.pin1
  N4: ADC1.CH3, S5.pin1
  N5: ADC1.CH4, S4.pin1
  N6: ADC1.CH5, S3.pin1
  N7: ADC1.CH6, S2.pin1
  N8: ADC1.DGND, ADC1.AGND, ADC2.DGND, ADC2.AGND, S9.pin2, S8.pin2, S7.pin2, S6.pin2, S5.pin2, S4.pin2, S3.pin2, S10.pin2, S2.pin2, S11.pin2, S12.pin2, S1.pin2, Transmitter.GND, Buzzer.pin1, R2.Pin_1, C1.-, ESP32.GND#13, ESP32.GND#31
  N9: ADC1.CS/SHDN, ESP32.IO15
  N10: ADC1.Din, ESP32.IO13
  N11: ADC1.Dout, ESP32.IO12
  N12: ADC1.CLK, ESP32.IO14
  VDD: ADC1.VREF, ADC1.VDD, ADC2.VREF, ADC2.VDD, S9.pin3, S8.pin3, S7.pin3, S6.pin3, S5.pin3, S4.pin3, S3.pin3, S10.pin3, S2.pin3, S11.pin3, S12.pin3, S1.pin3, ESP32.3V3
  N13: ADC2.CH3, S1.pin1
  N14: ADC2.CH4, S12.pin1
  N15: ADC2.CH5, S11.pin1
  N16: ADC2.CH6, S10.pin1
  N17: ADC2.CH7, S9.pin1
  N18: ADC2.CS/SHDN, ESP32.IO5
  N19: ADC2.Din, ESP32.IO23
  N20: ADC2.Dout, ESP32.IO19
  N21: ADC2.CLK, ESP32.IO18
  N22: Transmitter.DATA, ESP32.IO17
  +5V: Transmitter.+5V, R3.Pin_0, ESP32.5V
  N23: Buzzer.pin2, ESP32.IO21
  N24: R2.Pin_0, R3.Pin_1, C1.+, SCT013.pin1, R1.Pin_1
  N25: SCT013.pin2, R1.Pin_0, ESP32.IO33

notes:
  3V3

custom parts:
  KY-026: ky-026 flame sensor module
  ESP32 DevKit C: The ESP32 is a WiFi and Bluetooth-enabled 32-bit, dual-core microcontroller.
