# Fritzing sketch sensorbox-final (saved by Fritzing 0.9.3b)

parts:
  WeMos_D1_Mini1 = WeMos D1 Mini
  Part1 = KY-002 Vibration Switch Module [package="Breakout board"]
  Part3 = KY-006 Passive Buzzer Module [package="Breakout board"]
  Part4 = KY-018 Photoresistor Module [package="Breakout board"]
  Flame_Sensor = KY-026
  Temperature_and_Humidity_Sensor = KY-015 Temperature & Humidity Sensor Module [package="Breakout board"]

nets:
  VIN: WeMos_D1_Mini1.5V, Part1.Vin, Part4.Vin, Flame_Sensor.pin3, Temperature_and_Humidity_Sensor.Vin
  N1: WeMos_D1_Mini1.A0, Part4.S
  N2: WeMos_D1_Mini1.D1, Part3.S
  N3: WeMos_D1_Mini1.D3, Part1.S
  N4: WeMos_D1_Mini1.D5, Temperature_and_Humidity_Sensor.S
  N5: WeMos_D1_Mini1.D7, Flame_Sensor.pin4
  N6: WeMos_D1_Mini1.G, Part1.-, Part3.-, Part4.-, Flame_Sensor.pin2, Temperature_and_Humidity_Sensor.-

notes:
  Passive Piezo Buzzer
  Shock Sensor
  Photo
  Cell
  Temperature and Humidity Sensor
  Flame Sensor

custom parts:
  KY-002 Vibration Switch Module: Arduino Vibration Switch Module KY-002 Keyes allows detection of shock and vibration.
  KY-006 Passive Buzzer Module: Passive Piezoelectric Buzzer Module Keyes KY-006, it can produce a range of sound tones depending on the input frequency.
  KY-018 Photoresistor Module: KY-018 Photoresistor module, used to measure light intensity. It can determine the presence or absence of light.
  KY-026: ky-026 flame sensor module
  KY-015 Temperature & Humidity Sensor Module: KY-015 temperature and humidity sensor module, provides a low-latency serial interface to measure humidity and temperature.
